// Digital circuit 5-bit_counter.dig as structural Verilog
module _5_bit_counter (
  input  clk,
  output a_3,
  output a_2,
  output a_1,
  output a_0,
  output a_4
);

  wire _7474_1_pin2, _7474_1_pin5, _74191_1_pin12, _74191_1_pin13;

  _74191 _74191_1 (
    .pin1(1'b0), .pin2(a_1), .pin3(a_0), .pin4(1'b0), .pin5(1'b0), .pin6(a_2), .pin7(a_3), .pin8(1'b0),
    .pin9(1'b0), .pin10(1'b0), .pin11(1'b1), .pin12(_74191_1_pin12), .pin13(_74191_1_pin13), .pin14(clk),
    .pin15(1'b0), .pin16(1'b1));
  _7474 _7474_1 (
    .pin1(1'b1), .pin2(_7474_1_pin2), .pin3(_74191_1_pin12), .pin4(1'b1), .pin5(_7474_1_pin5),
    .pin6(_7474_1_pin2), .pin7(1'b0), .pin9(a_4), .pin10(1'b1), .pin11(_74191_1_pin13), .pin12(_7474_1_pin5),
    .pin13(1'b1), .pin14(1'b1));  // open: pin8

  // Notes on the sheet:
  //   clk: Hz: 5
endmodule
