// Digital circuit ALU.dig as structural Verilog
module ALU (
  input  A_0,
  input  A_1,
  input  B_0,
  input  B_1,
  input  ADD,
  input  AND,
  input  OR,
  input  SUB,
  output C,
  output Q_0,
  output Q_1
);

  wire not_1_out, or_1_out, xor_1_out, xor_2_out;
  wire [1:0] _7483_1_pin6, and_1_out, or_2_out;

  or or_1 (or_1_out, SUB, ADD);
  not not_1 (not_1_out, ADD);
  xor xor_1 (xor_1_out, not_1_out, B_0);
  xor xor_2 (xor_2_out, not_1_out, B_1);
  _7483 _7483_1 (
    .pin1(1'b0), .pin2(C), .pin3(1'b0), .pin4(not_1_out), .pin5(1'b1), .pin6(_7483_1_pin6[1]),
    .pin7(xor_2_out), .pin8(A_1), .pin9(_7483_1_pin6[0]), .pin10(A_0), .pin11(xor_1_out), .pin12(1'b0),
    .pin13(not_1_out), .pin16(not_1_out));  // open: pin14, pin15
  or or_2 (or_2_out[1], A_0, B_1);
  or or_3 (or_2_out[0], B_0, B_1);
  and and_1 (and_1_out[1], A_0, B_0);
  and and_2 (and_1_out[0], A_1, B_1);
  assign {Q_1, Q_0} = AND ? and_1_out : 2'bz;  // Driver driver_1
  assign {Q_1, Q_0} = OR ? or_2_out : 2'bz;  // Driver driver_2
  assign {Q_1, Q_0} = or_1_out ? _7483_1_pin6 : 2'bz;  // Driver driver_3
endmodule
