// Digital circuit DATARAM.dig as structural Verilog
module DATARAM (
  input  WE,
  input  a_1,
  input  a_0,
  input  en,
  input  RE,
  output D_0,
  output D_1
);

  wire _74238_1_pin12, _74238_1_pin13, _74238_1_pin14, _74238_1_pin15, _74373_1_pin11, _74373_2_pin11,
       _74373_3_pin11, _74373_4_pin11, nand_1_out, nand_2_out, nand_3_out, nand_4_out;

  _74238 _74238_1 (
    .pin1(a_0), .pin2(a_1), .pin3(1'b0), .pin4(1'b0), .pin5(1'b0), .pin6(en), .pin8(1'b0),
    .pin12(_74238_1_pin12), .pin13(_74238_1_pin13), .pin14(_74238_1_pin14), .pin15(_74238_1_pin15),
    .pin16(1'b1));  // open: pin7, pin9, pin10, pin11
  nand nand_1 (nand_1_out, RE, _74238_1_pin15);
  nand nand_2 (nand_2_out, RE, _74238_1_pin14);
  nand nand_3 (nand_3_out, RE, _74238_1_pin13);
  nand nand_4 (nand_4_out, RE, _74238_1_pin12);
  _74373 _74373_1 (
    .pin1(nand_1_out), .pin2(D_0), .pin3(D_0), .pin4(D_1), .pin5(D_1), .pin7(1'b0), .pin8(1'b0),
    .pin10(1'b0), .pin11(_74373_1_pin11), .pin13(1'b0), .pin14(1'b0), .pin17(1'b0), .pin18(1'b0), .pin20(1'b1));  // open: pin6, pin9, pin12, pin15, pin16, pin19
  _74373 _74373_2 (
    .pin1(nand_2_out), .pin2(D_0), .pin3(D_0), .pin4(D_1), .pin5(D_1), .pin7(1'b0), .pin8(1'b0),
    .pin10(1'b0), .pin11(_74373_2_pin11), .pin13(1'b0), .pin14(1'b0), .pin17(1'b0), .pin18(1'b0), .pin20(1'b1));  // open: pin6, pin9, pin12, pin15, pin16, pin19
  _74373 _74373_3 (
    .pin1(nand_3_out), .pin2(D_0), .pin3(D_0), .pin4(D_1), .pin5(D_1), .pin7(1'b0), .pin8(1'b0),
    .pin10(1'b0), .pin11(_74373_3_pin11), .pin13(1'b0), .pin14(1'b0), .pin17(1'b0), .pin18(1'b0), .pin20(1'b1));  // open: pin6, pin9, pin12, pin15, pin16, pin19
  _74373 _74373_4 (
    .pin1(nand_4_out), .pin2(D_0), .pin3(D_0), .pin4(D_1), .pin5(D_1), .pin7(1'b0), .pin8(1'b0),
    .pin10(1'b0), .pin11(_74373_4_pin11), .pin13(1'b0), .pin14(1'b0), .pin17(1'b0), .pin18(1'b0), .pin20(1'b1));  // open: pin6, pin9, pin12, pin15, pin16, pin19
  and and_1 (_74373_1_pin11, WE, _74238_1_pin15);
  and and_2 (_74373_2_pin11, WE, _74238_1_pin14);
  and and_3 (_74373_3_pin11, WE, _74238_1_pin13);
  and and_4 (_74373_4_pin11, WE, _74238_1_pin12);

  // Notes on the sheet:
  //   en: default 1
endmodule
