// Digital circuit General_Register_File.dig as structural Verilog
module General_Register_File (
  input  D_1,
  input  D_0,
  input  REG,
  input  W,
  input  OE,
  output A_1,
  output A_0,
  output B_0,
  output B_1
);

  wire and_1_out, and_2_out, not_1_out, not_2_out;

  not not_1 (not_1_out, REG);
  not not_2 (not_2_out, OE);
  and and_1 (and_1_out, W, not_1_out);
  and and_2 (and_2_out, W, REG);
  _74373 _74373_1 (
    .pin1(not_2_out), .pin2(A_0), .pin3(D_0), .pin4(D_1), .pin5(A_1), .pin7(1'b0), .pin8(1'b0), .pin10(1'b0),
    .pin11(and_1_out), .pin13(1'b0), .pin14(1'b0), .pin17(1'b0), .pin18(1'b0), .pin20(1'b1));  // open: pin6, pin9, pin12, pin15, pin16, pin19
  _74373 _74373_2 (
    .pin1(not_2_out), .pin2(B_0), .pin3(D_0), .pin4(D_1), .pin5(B_1), .pin7(1'b0), .pin8(1'b0), .pin10(1'b0),
    .pin11(and_2_out), .pin13(1'b0), .pin14(1'b0), .pin17(1'b0), .pin18(1'b0), .pin20(1'b1));  // open: pin6, pin9, pin12, pin15, pin16, pin19
endmodule
