// Digital circuit instr_load.dig as structural Verilog
module instr_load (
  input  en,
  input  in_6,
  input  clk,
  output eax_1,
  output eax_0,
  output ebx_0,
  output ebx_1,
  output Carry,
  output [7:0] out_9,
  output [4:0] out_10,
  output CLK_2
);

  wire _74238_1_pin7, _74238_1_pin10, _74238_1_pin11, _74238_1_pin12, _74238_1_pin13, _74238_1_pin14,
       _74238_1_pin15, alu_1_q_0, alu_1_q_1, and_1_out, and_2_out, and_3_out, and_4_out, dataram_1_d_1,
       driver_1_out, driver_2_out, nand_1_out, not_1_out, not_2_out, not_3_out, or_1_out, or_2_out;

  _74238 _74238_1 (
    .pin1(out_9[5]), .pin2(out_9[6]), .pin3(out_9[7]), .pin4(1'b0), .pin5(1'b0), .pin6(en),
    .pin7(_74238_1_pin7), .pin8(1'b0), .pin10(_74238_1_pin10), .pin11(_74238_1_pin11),
    .pin12(_74238_1_pin12), .pin13(_74238_1_pin13), .pin14(_74238_1_pin14), .pin15(_74238_1_pin15),
    .pin16(1'b1));  // open: pin9
  nand nand_1 (nand_1_out, _74238_1_pin14, out_9[4]);
  assign driver_1_out = not_1_out ? out_9[3] : 1'bz;  // Driver driver_1
  not not_1 (not_1_out, out_9[4]);
  assign driver_2_out = not_1_out ? out_9[2] : 1'bz;  // Driver driver_2
  assign driver_2_out = _74238_1_pin15 ? out_9[2] : 1'bz;  // Driver driver_3
  not not_2 (not_2_out, _74238_1_pin7);
  Counter #(.Bits(5)) counter_1 (.en(not_2_out), .C(clk), .clr(in_6), .out(out_10));  // open: ovf
  and and_1 (and_1_out, _74238_1_pin14, not_1_out);
  or or_1 (or_1_out, _74238_1_pin15, _74238_1_pin14);
  ROM #(.AddrBits(5), .Bits(8)) rom_1 (.A(out_10), .sel(1'b1), .D(out_9));
  and and_2 (and_2_out, not_3_out, _74238_1_pin14);
  DATARAM dataram_1 (
    .WE(and_2_out), .a_1(out_9[1]), .a_0(out_9[0]), .en(or_1_out), .RE(_74238_1_pin15), .D_0(driver_1_out),
    .D_1(dataram_1_d_1));
  not not_3 (not_3_out, clk);
  assign dataram_1_d_1 = and_1_out ? driver_2_out : 1'bz;  // Driver driver_4
  and and_3 (and_3_out, _74238_1_pin15, not_3_out);
  General_Register_File general_register_file_1 (
    .D_1(driver_1_out), .D_0(dataram_1_d_1), .REG(driver_2_out), .W(and_3_out), .OE(1'b1), .A_1(eax_1),
    .A_0(eax_0), .B_0(ebx_0), .B_1(ebx_1));
  or or_2 (or_2_out, _74238_1_pin10, _74238_1_pin11, _74238_1_pin12, _74238_1_pin13);
  ALU alu_1 (
    .A_0(eax_0), .A_1(eax_1), .B_0(ebx_0), .B_1(ebx_1), .ADD(_74238_1_pin13), .AND(_74238_1_pin12),
    .OR(_74238_1_pin11), .SUB(_74238_1_pin10), .C(Carry), .Q_0(alu_1_q_0), .Q_1(alu_1_q_1));
  and and_4 (and_4_out, or_2_out, not_3_out);
  _74373 _74373_1 (
    .pin1(nand_1_out), .pin2(driver_1_out), .pin3(alu_1_q_0), .pin4(alu_1_q_1), .pin5(dataram_1_d_1),
    .pin7(1'b0), .pin8(1'b0), .pin10(1'b0), .pin11(and_4_out), .pin13(1'b0), .pin14(1'b0), .pin17(1'b0),
    .pin18(1'b0), .pin20(1'b1));  // open: pin6, pin9, pin12, pin15, pin16, pin19

  assign CLK_2 = clk;

  // Notes on the sheet:
  //   en: default 1
  //   contents of rom_1 (hex, n*v repeats v):
  //   24,29,2e,10,16,40,33,12,14,a0,30,13,32,13,14,80,32,12,15,60,33
  //   ,13,e0
endmodule
